# Fritzing sketch EL_GP (saved by Fritzing 0.9.3b)

parts:
  Raspberry_Pi1 = Raspberry Pi B+
  IC1 = PICAXE-40X1 [package=THT]
  Part3 = Arduino Uno (Rev3) - ICSP
  M1 = DC Motor
  M2 = DC Motor
  Part4 = Motor Driver 1A Dual TB6612FNG
  U1 = LIPO-2000mAh [package=lipo-2000]
  J2 = Basic Servo
  J3 = Basic Servo  # not connected
  IC2 = PICAXE-40X1 [package=THT]
  hc-sr1 = hc-sr04
  IC3 = PICAXE-40X1 [package=THT]
  J5 = Basic Servo
  hc-sr2 = hc-sr04
  hc-sr3 = hc-sr04
  hc-sr4 = hc-sr04
  U2 = LIPO-2000mAh [package=lipo-2000]
  J4 = Basic Servo
  U4 = TRANSCHIPTC5747 [package=camera_sfv24r-2st_2]
  M3 = DC Motor
  M4 = DC Motor
  Part5 = Motor Driver 1A Dual TB6612FNG
  M6 = DC Motor
  M7 = DC Motor
  M8 = DC Motor
  M5 = DC Motor
  Q1 = Basic FET P-Channel [package="TO220 [THT]"]  # not connected
  LED2 = RGB LED (com. cathode, rgb) [package="5 mm [THT]"]  # not connected
  LED3 = RGB LED (com. cathode, rgb) [package="5 mm [THT]"]  # not connected
  LED4 = RGB LED (com. cathode, rgb) [package="5 mm [THT]"]  # not connected
  LED5 = RGB LED (com. cathode, rgb) [package="5 mm [THT]"]  # not connected
  J6 = Piezo Speaker  # not connected
  Part6 = Bluetooth HC-05 Macho  # not connected

nets:
  N1: Raspberry_Pi1.GPIO8, U4.DOUT_5
  N2: Raspberry_Pi1.GPIO25, U4.DOUT_4
  N3: Raspberry_Pi1.GND, U4.AVDD28, U4.DOUT_0, U4.DOUT_3
  N4: Raspberry_Pi1.GPIO24, U4.DOUT_2
  N5: Raspberry_Pi1.GPIO23, U4.DOUT_1
  N6: Raspberry_Pi1.GPIO18, U4.DGND
  N7: Raspberry_Pi1.GPIO15, U4.CLK_IN
  N8: Raspberry_Pi1.GPIO14, U4.RESET_N
  N9: Raspberry_Pi1.5V, U4.SCLK, U4.AGND
  N10: IC1.In_A2_/_ADC_2, U2.-, Part5.GND
  N11: IC1.In_A3_/_ADC_3, Part5.VCC
  N12: IC1.Serial_In, Part5.VM
  N13: IC1.Resonator_(_Optional_)#12, Part5.PWMA
  N14: IC1.Resonator_(_Optional_)#13, Part5.AIN2
  N15: IC1.In/Out_C0_/_Timer_Clock, Part5.AIN1
  N16: IC1.In_2, IC2.In_2, IC3.In_2
  N17: IC1.In_3, IC2.In_3, IC3.In_3
  N18: IC1.In/Out_C4_/_I2C_Data_/_SPI_Data_In, IC2.In/Out_C4_/_I2C_Data_/_SPI_Data_In, IC3.In/Out_C4_/_I2C_Data_/_SPI_Data_In
  N19: IC1.In/Out_C5_/_SPI_Data_Out, IC2.In/Out_C5_/_SPI_Data_Out, IC3.In/Out_C5_/_SPI_Data_Out
  N20: Part3.D0/RX, Part4.GND, U1.-
  N21: Part3.D1/TX, Part4.VCC
  N22: Part3.D2, Part4.VM
  N23: Part3.D4, Part4.PWMA
  N24: Part3.D5_PWM, Part4.AIN2
  N25: Part3.D6_PWM, Part4.AIN1
  N26: M1.pin_1, Part4.STBY, M3.pin_1
  N27: M1.pin_2, Part4.BIN1, M3.pin_2
  N28: M2.pin_1, Part4.B02, M4.pin_1
  N29: Part4.B01, U1.+
  GND: J2.gnd, hc-sr2.GND
  VCC: J2.vcc, hc-sr2.VCC
  N30: IC2.ADC_6, hc-sr3.Echo
  N31: IC2.+V, hc-sr2.Echo, hc-sr3.Trig
  N32: IC2.Out_2, hc-sr2.Trig
  VCC_2: hc-sr1.VCC, J5.vcc, hc-sr3.VCC, hc-sr4.VCC, J4.vcc
  N33: hc-sr1.Trig, IC3.Out_6
  N34: hc-sr1.Echo, IC3.Out_4
  GND_2: hc-sr1.GND, J5.gnd, hc-sr3.GND, hc-sr4.GND, J4.gnd
  N35: IC3.In_A2_/_ADC_2, hc-sr4.Echo
  N36: IC3.Serial_In, hc-sr4.Trig
  N37: U2.+, Part5.B01
  N38: Part5.A02, M7.pin_2, M8.pin_2
  N39: Part5.A01, M7.pin_1, M8.pin_1
  N40: Part5.STBY, M6.pin_1, M5.pin_1
  N41: Part5.BIN1, M6.pin_2, M5.pin_2
